// Logisim project EXP2.circ as structural Verilog: 1 circuit, main circuit main
module main (
  input  As,
  input  Bs,
  input  Mode,
  input  [6:0] Zeros,
  input  [6:0] A,
  input  [6:0] B,
  input  [6:0] Zeros_2,
  output s,
  output Calling_control,
  output [6:0] Result_A,
  output E,
  output [6:0] Final_A,
  output Final_As,
  output AVS
);

  wire comparator_1_eq, multiplexer_2_out, multiplexer_4_out, not_3_out;
  wire [6:0] adder_2_out, multiplexer_1_out, multiplexer_3_out, not_1_out, not_2_out;

  xor xor_1 (s, As, Bs);
  Comparator #(.width(7)) comparator_1 (.a(Result_A), .b(Zeros_2), .eq(comparator_1_eq));  // open: gt, lt
  Multiplexer #(.width(7), .enable("false")) multiplexer_1 (
    .in0(B), .in1(not_1_out), .out(multiplexer_1_out), .sel(Calling_control));
  assign not_1_out = ~B;  // NOT_Gate not_1, 7 bits wide
  Multiplexer #(.enable("false")) multiplexer_2 (.in0(As), .in1(1'b0), .out(multiplexer_2_out), .sel(comparator_1_eq));
  xor xor_2 (Calling_control, s, Mode);
  Adder #(.width(7)) adder_1 (.a(A), .b(multiplexer_1_out), .out(Result_A), .cin(Calling_control), .cout(E));
  assign not_2_out = ~Result_A;  // NOT_Gate not_2, 7 bits wide
  Adder #(.width(7)) adder_2 (.a(Zeros), .b(not_2_out), .out(adder_2_out), .cin(Calling_control));  // open: cout
  not not_3 (not_3_out, As);
  Multiplexer #(.width(7), .enable("false")) multiplexer_3 (
    .in0(adder_2_out), .in1(Result_A), .out(multiplexer_3_out), .sel(E));
  Multiplexer #(.enable("false")) multiplexer_4 (
    .in0(not_3_out), .in1(multiplexer_2_out), .out(multiplexer_4_out), .sel(E));
  Multiplexer #(.width(7), .enable("false")) multiplexer_5 (
    .in0(Result_A), .in1(multiplexer_3_out), .out(Final_A), .sel(Calling_control));
  Multiplexer #(.enable("false")) multiplexer_6 (
    .in0(As), .in1(multiplexer_4_out), .out(Final_As), .sel(Calling_control));
  Multiplexer #(.enable("false")) multiplexer_7 (.in0(E), .in1(1'b0), .out(AVS), .sel(Calling_control));

  // Notes on the sheet:
  //   As and Bs are sign bit of A and B respectively
  //   If Mode = 0 : Addition
  //   else Mode = 1 : Subtraction
  //   23CS037
  //   Magnitude of A and B
  //   If s = 0 : Same sign else diff.
  //   If calling control = 0 : call Func 1 : Add magnitude and use sign of A else call Func 2 : Sub smaller num from larger and use sign of larger num
endmodule
