// Logisim project EXP3.circ as structural Verilog: 4 circuits, main circuit Multiplexer
module Multiplexer (
  input  [1:0] in_1,
  input  [3:0] A,
  input  [3:0] B,
  input  [3:0] C,
  input  [3:0] D,
  input  in_6,
  output [3:0] out_7,
  output [3:0] out_8,
  output [3:0] out_9,
  output [3:0] out_10,
  output [3:0] out_11
);

  wire clock_1_out;

  Clock clock_1 (.out(clock_1_out));
  Multiplexer_part #(.select(2), .enable("false")) multiplexer_1 (
    .in0(out_8[3]), .in1(out_9[3]), .in2(out_10[3]), .in3(out_11[3]), .out(out_7[3]), .sel(in_1));
  Register #(.width(4)) register_1 (.D(A), .en(1'b1), .Q(out_8), .clk(clock_1_out), .clr(in_6));
  Multiplexer_part #(.select(2), .enable("false")) multiplexer_2 (
    .in0(out_8[2]), .in1(out_9[2]), .in2(out_10[2]), .in3(out_11[2]), .out(out_7[2]), .sel(in_1));
  Register #(.width(4)) register_2 (.D(B), .en(1'b1), .Q(out_9), .clk(clock_1_out), .clr(in_6));
  Multiplexer_part #(.select(2), .enable("false")) multiplexer_3 (
    .in0(out_8[1]), .in1(out_9[1]), .in2(out_10[1]), .in3(out_11[1]), .out(out_7[1]), .sel(in_1));
  Register #(.width(4)) register_3 (.D(C), .en(1'b1), .Q(out_10), .clk(clock_1_out), .clr(in_6));
  Multiplexer_part #(.select(2), .enable("false")) multiplexer_4 (
    .in0(out_8[0]), .in1(out_9[0]), .in2(out_10[0]), .in3(out_11[0]), .out(out_7[0]), .sel(in_1));
  Register #(.width(4)) register_4 (.D(D), .en(1'b1), .Q(out_11), .clk(clock_1_out), .clr(in_6));

  // Notes on the sheet:
  //   23CS037
endmodule

module Tristate (
  input  [1:0] in_1,
  input  [3:0] A,
  input  [3:0] B,
  input  [3:0] C,
  input  [3:0] D,
  input  in_6,
  output [3:0] out_7,
  output [3:0] out_8,
  output [3:0] out_9,
  output [3:0] out_10,
  output [3:0] out_11
);

  wire clock_1_out, decoder_1_out0, decoder_1_out1, decoder_1_out2, decoder_1_out3;

  Decoder #(.select(2), .enable("false")) decoder_1 (
    .out0(decoder_1_out0), .out1(decoder_1_out1), .out2(decoder_1_out2), .out3(decoder_1_out3), .sel(in_1));
  Clock clock_1 (.out(clock_1_out));
  assign out_7[3] = decoder_1_out0 ? out_8[3] : 1'bz;  // Controlled_Buffer A
  assign out_7[3] = decoder_1_out1 ? out_9[3] : 1'bz;  // Controlled_Buffer B
  assign out_7[3] = decoder_1_out2 ? out_10[3] : 1'bz;  // Controlled_Buffer C
  assign out_7[3] = decoder_1_out3 ? out_11[3] : 1'bz;  // Controlled_Buffer D
  Register #(.width(4)) register_1 (.D(A), .en(1'b1), .Q(out_8), .clk(clock_1_out), .clr(in_6));
  assign out_7[2] = decoder_1_out0 ? out_8[2] : 1'bz;  // Controlled_Buffer controlled_buffer_1
  assign out_7[2] = decoder_1_out1 ? out_9[2] : 1'bz;  // Controlled_Buffer controlled_buffer_2
  assign out_7[2] = decoder_1_out2 ? out_10[2] : 1'bz;  // Controlled_Buffer controlled_buffer_3
  assign out_7[2] = decoder_1_out3 ? out_11[2] : 1'bz;  // Controlled_Buffer controlled_buffer_4
  Register #(.width(4)) register_2 (.D(B), .en(1'b1), .Q(out_9), .clk(clock_1_out), .clr(in_6));
  assign out_7[1] = decoder_1_out0 ? out_8[1] : 1'bz;  // Controlled_Buffer controlled_buffer_5
  assign out_7[1] = decoder_1_out1 ? out_9[1] : 1'bz;  // Controlled_Buffer controlled_buffer_6
  assign out_7[1] = decoder_1_out2 ? out_10[1] : 1'bz;  // Controlled_Buffer controlled_buffer_7
  assign out_7[1] = decoder_1_out3 ? out_11[1] : 1'bz;  // Controlled_Buffer controlled_buffer_8
  assign out_7[0] = decoder_1_out0 ? out_8[0] : 1'bz;  // Controlled_Buffer controlled_buffer_9
  assign out_7[0] = decoder_1_out1 ? out_9[0] : 1'bz;  // Controlled_Buffer controlled_buffer_10
  assign out_7[0] = decoder_1_out2 ? out_10[0] : 1'bz;  // Controlled_Buffer controlled_buffer_11
  assign out_7[0] = decoder_1_out3 ? out_11[0] : 1'bz;  // Controlled_Buffer controlled_buffer_12
  Register #(.width(4)) register_3 (.D(C), .en(1'b1), .Q(out_10), .clk(clock_1_out), .clr(in_6));
  Register #(.width(4)) register_4 (.D(D), .en(1'b1), .Q(out_11), .clk(clock_1_out), .clr(in_6));

  // Notes on the sheet:
  //   23CS037
endmodule

module postSessionMultiplexer (
  input  [1:0] in_1,
  input  [4:0] A,
  input  [4:0] B,
  input  [4:0] C,
  input  [4:0] D,
  input  in_6,
  output [4:0] out_7,
  output [4:0] out_8,
  output [4:0] out_9,
  output [4:0] out_10,
  output [4:0] out_11
);

  wire clock_1_out;

  Multiplexer_part #(.select(2), .enable("false")) multiplexer_1 (
    .in0(out_8[4]), .in1(out_9[4]), .in2(out_10[4]), .in3(out_11[4]), .out(out_7[4]), .sel(in_1));
  Clock clock_1 (.out(clock_1_out));
  Multiplexer_part #(.select(2), .enable("false")) multiplexer_2 (
    .in0(out_8[3]), .in1(out_9[3]), .in2(out_10[3]), .in3(out_11[3]), .out(out_7[3]), .sel(in_1));
  Register #(.width(5)) register_1 (.D(A), .en(1'b1), .Q(out_8), .clk(clock_1_out), .clr(in_6));
  Multiplexer_part #(.select(2), .enable("false")) multiplexer_3 (
    .in0(out_8[2]), .in1(out_9[2]), .in2(out_10[2]), .in3(out_11[2]), .out(out_7[2]), .sel(in_1));
  Register #(.width(5)) register_2 (.D(B), .en(1'b1), .Q(out_9), .clk(clock_1_out), .clr(in_6));
  Multiplexer_part #(.select(2), .enable("false")) multiplexer_4 (
    .in0(out_8[1]), .in1(out_9[1]), .in2(out_10[1]), .in3(out_11[1]), .out(out_7[1]), .sel(in_1));
  Register #(.width(5)) register_3 (.D(C), .en(1'b1), .Q(out_10), .clk(clock_1_out), .clr(in_6));
  Multiplexer_part #(.select(2), .enable("false")) multiplexer_5 (
    .in0(out_8[0]), .in1(out_9[0]), .in2(out_10[0]), .in3(out_11[0]), .out(out_7[0]), .sel(in_1));
  Register #(.width(5)) register_4 (.D(D), .en(1'b1), .Q(out_11), .clk(clock_1_out), .clr(in_6));

  // Notes on the sheet:
  //   23CS037
endmodule

module postSessionTristate (
  input  [1:0] in_1,
  input  [4:0] A,
  input  [4:0] B,
  input  [4:0] C,
  input  [4:0] D,
  input  in_6,
  output [4:0] out_7,
  output [4:0] out_8,
  output [4:0] out_9,
  output [4:0] out_10,
  output [4:0] out_11
);

  wire clock_1_out, decoder_1_out0, decoder_1_out1, decoder_1_out2, decoder_1_out3;

  Decoder #(.select(2), .enable("false")) decoder_1 (
    .out0(decoder_1_out0), .out1(decoder_1_out1), .out2(decoder_1_out2), .out3(decoder_1_out3), .sel(in_1));
  assign out_7[4] = decoder_1_out0 ? out_8[4] : 1'bz;  // Controlled_Buffer controlled_buffer_1
  assign out_7[4] = decoder_1_out1 ? out_9[4] : 1'bz;  // Controlled_Buffer controlled_buffer_2
  assign out_7[4] = decoder_1_out2 ? out_10[4] : 1'bz;  // Controlled_Buffer controlled_buffer_3
  assign out_7[4] = decoder_1_out3 ? out_11[4] : 1'bz;  // Controlled_Buffer controlled_buffer_4
  Clock clock_1 (.out(clock_1_out));
  assign out_7[3] = decoder_1_out0 ? out_8[3] : 1'bz;  // Controlled_Buffer controlled_buffer_5
  assign out_7[3] = decoder_1_out1 ? out_9[3] : 1'bz;  // Controlled_Buffer controlled_buffer_6
  assign out_7[3] = decoder_1_out2 ? out_10[3] : 1'bz;  // Controlled_Buffer controlled_buffer_7
  assign out_7[3] = decoder_1_out3 ? out_11[3] : 1'bz;  // Controlled_Buffer controlled_buffer_8
  Register #(.width(5)) register_1 (.D(A), .en(1'b1), .Q(out_8), .clk(clock_1_out), .clr(in_6));
  assign out_7[2] = decoder_1_out0 ? out_8[2] : 1'bz;  // Controlled_Buffer controlled_buffer_9
  assign out_7[2] = decoder_1_out1 ? out_9[2] : 1'bz;  // Controlled_Buffer controlled_buffer_10
  assign out_7[2] = decoder_1_out2 ? out_10[2] : 1'bz;  // Controlled_Buffer controlled_buffer_11
  assign out_7[2] = decoder_1_out3 ? out_11[2] : 1'bz;  // Controlled_Buffer controlled_buffer_12
  assign out_7[1] = decoder_1_out0 ? out_8[1] : 1'bz;  // Controlled_Buffer controlled_buffer_13
  assign out_7[1] = decoder_1_out1 ? out_9[1] : 1'bz;  // Controlled_Buffer controlled_buffer_14
  assign out_7[1] = decoder_1_out2 ? out_10[1] : 1'bz;  // Controlled_Buffer controlled_buffer_15
  assign out_7[1] = decoder_1_out3 ? out_11[1] : 1'bz;  // Controlled_Buffer controlled_buffer_16
  Register #(.width(5)) register_2 (.D(B), .en(1'b1), .Q(out_9), .clk(clock_1_out), .clr(in_6));
  assign out_7[0] = decoder_1_out0 ? out_8[0] : 1'bz;  // Controlled_Buffer controlled_buffer_17
  assign out_7[0] = decoder_1_out1 ? out_9[0] : 1'bz;  // Controlled_Buffer controlled_buffer_18
  assign out_7[0] = decoder_1_out2 ? out_10[0] : 1'bz;  // Controlled_Buffer controlled_buffer_19
  assign out_7[0] = decoder_1_out3 ? out_11[0] : 1'bz;  // Controlled_Buffer controlled_buffer_20
  Register #(.width(5)) register_3 (.D(C), .en(1'b1), .Q(out_10), .clk(clock_1_out), .clr(in_6));
  Register #(.width(5)) register_4 (.D(D), .en(1'b1), .Q(out_11), .clk(clock_1_out), .clr(in_6));

  // Notes on the sheet:
  //   23CS037
endmodule
