// Logisim project EXP4 & EXP5.circ as structural Verilog: 19 circuits, main circuit 1bit-Arithmatic
module _1bit_Arithmatic (
  input  Cin,
  input  A0,
  input  B0,
  input  [1:0] in_4,
  output S0,
  output Cout
);

  wire multiplexer_1_out, not_1_out;

  not not_1 (not_1_out, B0);
  Multiplexer #(.select(2), .enable("false")) multiplexer_1 (
    .in0(B0), .in1(not_1_out), .in2(1'b0), .in3(1'b1), .out(multiplexer_1_out), .sel(in_4));
  Adder #(.width(1)) adder_1 (.a(A0), .b(multiplexer_1_out), .out(S0), .cin(Cin), .cout(Cout));

  // Notes on the sheet:
  //   23CS037
  //   1 bit and 4bit
endmodule

module _1bit_Logical_4 (
  input  A0,
  input  B0,
  input  [1:0] in_3,
  output Y0
);

  wire and_1_out, not_1_out, or_1_out, xor_1_out;

  and and_1 (and_1_out, A0, B0);
  or or_1 (or_1_out, A0, B0);
  xor xor_1 (xor_1_out, A0, B0);
  not not_1 (not_1_out, A0);
  Multiplexer #(.select(2), .enable("false")) multiplexer_1 (
    .in0(and_1_out), .in1(or_1_out), .in2(xor_1_out), .in3(not_1_out), .out(Y0), .sel(in_3));

  // Notes on the sheet:
  //   23CS037
endmodule

module _1bit_Logical_16 (
  input  B,
  input  A,
  input  [3:0] in_3,
  output F
);

  wire and_1_out, and_2_out, and_3_out, and_4_out, nand_1_out, nor_1_out, not_1_out, not_2_out, or_1_out,
       or_2_out, or_3_out, or_4_out, xnor_1_out, xor_1_out;

  not not_1 (not_1_out, B);
  not not_2 (not_2_out, A);
  and and_1 (and_1_out, A, 1'b0);
  and and_2 (and_2_out, A, B);
  and and_3 (and_3_out, A, not_1_out);
  and and_4 (and_4_out, not_2_out, B);
  xor xor_1 (xor_1_out, A, B);
  or or_1 (or_1_out, A, B);
  nor nor_1 (nor_1_out, A, B);
  xnor xnor_1 (xnor_1_out, A, B);
  or or_2 (or_2_out, A, not_1_out);
  or or_3 (or_3_out, not_2_out, B);
  nand nand_1 (nand_1_out, A, B);
  or or_4 (or_4_out, A, 1'b1);
  Multiplexer #(.select(4), .enable("false")) multiplexer_1 (
    .in0(and_1_out), .in1(and_2_out), .in2(and_3_out), .in3(A), .in4(and_4_out), .in5(B), .in6(xor_1_out),
    .in7(or_1_out), .in8(nor_1_out), .in9(xnor_1_out), .in10(not_1_out), .in11(or_2_out), .in12(not_2_out),
    .in13(or_3_out), .in14(nand_1_out), .in15(or_4_out), .out(F), .sel(in_3));

  // Notes on the sheet:
  //   23CS037
endmodule

module _2bit_biDirectionalShifter (
  input  [1:0] A1_A0,
  input  Select,
  output [1:0] F
);

  Multiplexer #(.enable("false")) multiplexer_1 (.in0(A1_A0[1]), .in1(1'b0), .out(F[0]), .sel(Select));
  Multiplexer #(.enable("false")) multiplexer_2 (.in0(1'b0), .in1(A1_A0[0]), .out(F[1]), .sel(Select));

  // Notes on the sheet:
  //   serialInputRight
  //   23CS037
  //   serialInputLeft
endmodule

module _2bit_Arithmatic (
  input  Cin,
  input  A0,
  input  B0,
  input  A1,
  input  B1,
  input  [1:0] in_6,
  output S0,
  output S1,
  output Cout
);

  wire adder_1_cout, multiplexer_1_out, multiplexer_2_out, not_1_out, not_2_out;

  not not_1 (not_1_out, B0);
  Multiplexer #(.select(2), .enable("false")) multiplexer_1 (
    .in0(B0), .in1(not_1_out), .in2(1'b0), .in3(1'b1), .out(multiplexer_1_out), .sel(in_6));
  not not_2 (not_2_out, B1);
  Multiplexer #(.select(2), .enable("false")) multiplexer_2 (
    .in0(B1), .in1(not_2_out), .in2(1'b0), .in3(1'b1), .out(multiplexer_2_out), .sel(in_6));
  Adder #(.width(1)) adder_1 (.a(A0), .b(multiplexer_1_out), .out(S0), .cin(Cin), .cout(adder_1_cout));
  Adder #(.width(1)) adder_2 (.a(A1), .b(multiplexer_2_out), .out(S1), .cin(adder_1_cout), .cout(Cout));

  // Notes on the sheet:
  //   23CS037
endmodule

module _4bit_Arithmatic (
  input  Cin,
  input  A0,
  input  B0,
  input  A1,
  input  B1,
  input  A2,
  input  B2,
  input  A3,
  input  B3,
  input  [1:0] in_10,
  output S0,
  output S1,
  output S2,
  output S3,
  output Cout
);

  wire adder_1_cout, adder_2_cout, adder_3_cout, multiplexer_1_out, multiplexer_2_out, multiplexer_3_out,
       multiplexer_4_out, not_1_out, not_2_out, not_3_out, not_4_out;

  not not_1 (not_1_out, B0);
  not not_2 (not_2_out, B1);
  not not_3 (not_3_out, B2);
  not not_4 (not_4_out, B3);
  Multiplexer #(.select(2), .enable("false")) multiplexer_1 (
    .in0(B0), .in1(not_1_out), .in2(1'b0), .in3(1'b1), .out(multiplexer_1_out), .sel(in_10));
  Multiplexer #(.select(2), .enable("false")) multiplexer_2 (
    .in0(B1), .in1(not_2_out), .in2(1'b0), .in3(1'b1), .out(multiplexer_2_out), .sel(in_10));
  Multiplexer #(.select(2), .enable("false")) multiplexer_3 (
    .in0(B2), .in1(not_3_out), .in2(1'b0), .in3(1'b1), .out(multiplexer_3_out), .sel(in_10));
  Multiplexer #(.select(2), .enable("false")) multiplexer_4 (
    .in0(B3), .in1(not_4_out), .in2(1'b0), .in3(1'b1), .out(multiplexer_4_out), .sel(in_10));
  Adder #(.width(1)) adder_1 (.a(A0), .b(multiplexer_1_out), .out(S0), .cin(Cin), .cout(adder_1_cout));
  Adder #(.width(1)) adder_2 (.a(A1), .b(multiplexer_2_out), .out(S1), .cin(adder_1_cout), .cout(adder_2_cout));
  Adder #(.width(1)) adder_3 (.a(A2), .b(multiplexer_3_out), .out(S2), .cin(adder_2_cout), .cout(adder_3_cout));
  Adder #(.width(1)) adder_4 (.a(A3), .b(multiplexer_4_out), .out(S3), .cin(adder_3_cout), .cout(Cout));

  // Notes on the sheet:
  //   23CS037
endmodule

module _8bit_Arithmatic (
  input  Cin,
  input  A0,
  input  B0,
  input  A1,
  input  B1,
  input  A2,
  input  B2,
  input  A3,
  input  B3,
  input  A4,
  input  B4,
  input  A5,
  input  B5,
  input  A6,
  input  B6,
  input  A7,
  input  B7,
  input  [1:0] in_18,
  output S0,
  output S1,
  output S2,
  output S3,
  output S4,
  output S5,
  output S6,
  output S7,
  output Cout
);

  wire adder_1_cout, adder_2_cout, adder_3_cout, adder_4_cout, adder_5_cout, adder_6_cout, adder_7_cout,
       multiplexer_1_out, multiplexer_2_out, multiplexer_3_out, multiplexer_4_out, multiplexer_5_out,
       multiplexer_6_out, multiplexer_7_out, multiplexer_8_out, not_1_out, not_2_out, not_3_out, not_4_out,
       not_5_out, not_6_out, not_7_out, not_8_out;

  not not_1 (not_1_out, B0);
  not not_2 (not_2_out, B1);
  not not_3 (not_3_out, B2);
  not not_4 (not_4_out, B3);
  not not_5 (not_5_out, B4);
  not not_6 (not_6_out, B5);
  not not_7 (not_7_out, B6);
  not not_8 (not_8_out, B7);
  Multiplexer #(.select(2), .enable("false")) multiplexer_1 (
    .in0(B0), .in1(not_1_out), .in2(1'b0), .in3(1'b1), .out(multiplexer_1_out), .sel(in_18));
  Multiplexer #(.select(2), .enable("false")) multiplexer_2 (
    .in0(B1), .in1(not_2_out), .in2(1'b0), .in3(1'b1), .out(multiplexer_2_out), .sel(in_18));
  Multiplexer #(.select(2), .enable("false")) multiplexer_3 (
    .in0(B2), .in1(not_3_out), .in2(1'b0), .in3(1'b1), .out(multiplexer_3_out), .sel(in_18));
  Multiplexer #(.select(2), .enable("false")) multiplexer_4 (
    .in0(B3), .in1(not_4_out), .in2(1'b0), .in3(1'b1), .out(multiplexer_4_out), .sel(in_18));
  Multiplexer #(.select(2), .enable("false")) multiplexer_5 (
    .in0(B4), .in1(not_5_out), .in2(1'b0), .in3(1'b1), .out(multiplexer_5_out), .sel(in_18));
  Multiplexer #(.select(2), .enable("false")) multiplexer_6 (
    .in0(B5), .in1(not_6_out), .in2(1'b0), .in3(1'b1), .out(multiplexer_6_out), .sel(in_18));
  Multiplexer #(.select(2), .enable("false")) multiplexer_7 (
    .in0(B6), .in1(not_7_out), .in2(1'b0), .in3(1'b1), .out(multiplexer_7_out), .sel(in_18));
  Multiplexer #(.select(2), .enable("false")) multiplexer_8 (
    .in0(B7), .in1(not_8_out), .in2(1'b0), .in3(1'b1), .out(multiplexer_8_out), .sel(in_18));
  Adder #(.width(1)) adder_1 (.a(A0), .b(multiplexer_1_out), .out(S0), .cin(Cin), .cout(adder_1_cout));
  Adder #(.width(1)) adder_2 (.a(A1), .b(multiplexer_2_out), .out(S1), .cin(adder_1_cout), .cout(adder_2_cout));
  Adder #(.width(1)) adder_3 (.a(A2), .b(multiplexer_3_out), .out(S2), .cin(adder_2_cout), .cout(adder_3_cout));
  Adder #(.width(1)) adder_4 (.a(A3), .b(multiplexer_4_out), .out(S3), .cin(adder_3_cout), .cout(adder_4_cout));
  Adder #(.width(1)) adder_5 (.a(A4), .b(multiplexer_5_out), .out(S4), .cin(adder_4_cout), .cout(adder_5_cout));
  Adder #(.width(1)) adder_6 (.a(A5), .b(multiplexer_6_out), .out(S5), .cin(adder_5_cout), .cout(adder_6_cout));
  Adder #(.width(1)) adder_7 (.a(A6), .b(multiplexer_7_out), .out(S6), .cin(adder_6_cout), .cout(adder_7_cout));
  Adder #(.width(1)) adder_8 (.a(A7), .b(multiplexer_8_out), .out(S7), .cin(adder_7_cout), .cout(Cout));

  // Notes on the sheet:
  //   23CS037
endmodule

module _2bit_Logical_4 (
  input  A0,
  input  B0,
  input  A1,
  input  B1,
  input  [1:0] in_5,
  output Y0,
  output Y1
);

  wire and_1_out, and_2_out, not_1_out, not_2_out, or_1_out, or_2_out, xor_1_out, xor_2_out;

  and and_1 (and_1_out, A0, B0);
  or or_1 (or_1_out, A0, B0);
  xor xor_1 (xor_1_out, A0, B0);
  not not_1 (not_1_out, A0);
  and and_2 (and_2_out, A1, B1);
  or or_2 (or_2_out, A1, B1);
  xor xor_2 (xor_2_out, A1, B1);
  not not_2 (not_2_out, A1);
  Multiplexer #(.select(2), .enable("false")) multiplexer_1 (
    .in0(and_1_out), .in1(or_1_out), .in2(xor_1_out), .in3(not_1_out), .out(Y0), .sel(in_5));
  Multiplexer #(.select(2), .enable("false")) multiplexer_2 (
    .in0(and_2_out), .in1(or_2_out), .in2(xor_2_out), .in3(not_2_out), .out(Y1), .sel(in_5));

  // Notes on the sheet:
  //   23CS037
endmodule

module _4bit_Logical_4 (
  input  A0,
  input  B0,
  input  A1,
  input  B1,
  input  A2,
  input  B2,
  input  A3,
  input  B3,
  input  [1:0] in_9,
  output Y0,
  output Y1,
  output Y2,
  output Y3
);

  wire and_1_out, and_2_out, and_3_out, and_4_out, not_1_out, not_2_out, not_3_out, not_4_out, or_1_out,
       or_2_out, or_3_out, or_4_out, xor_1_out, xor_2_out, xor_3_out, xor_4_out;

  and and_1 (and_1_out, A0, B0);
  or or_1 (or_1_out, A0, B0);
  xor xor_1 (xor_1_out, A0, B0);
  not not_1 (not_1_out, A0);
  and and_2 (and_2_out, A1, B1);
  or or_2 (or_2_out, A1, B1);
  xor xor_2 (xor_2_out, A1, B1);
  not not_2 (not_2_out, A1);
  and and_3 (and_3_out, A2, B2);
  or or_3 (or_3_out, A2, B2);
  xor xor_3 (xor_3_out, A2, B2);
  not not_3 (not_3_out, A2);
  and and_4 (and_4_out, A3, B3);
  or or_4 (or_4_out, A3, B3);
  xor xor_4 (xor_4_out, A3, B3);
  not not_4 (not_4_out, A3);
  Multiplexer #(.select(2), .enable("false")) multiplexer_1 (
    .in0(and_1_out), .in1(or_1_out), .in2(xor_1_out), .in3(not_1_out), .out(Y0), .sel(in_9));
  Multiplexer #(.select(2), .enable("false")) multiplexer_2 (
    .in0(and_2_out), .in1(or_2_out), .in2(xor_2_out), .in3(not_2_out), .out(Y1), .sel(in_9));
  Multiplexer #(.select(2), .enable("false")) multiplexer_3 (
    .in0(and_3_out), .in1(or_3_out), .in2(xor_3_out), .in3(not_3_out), .out(Y2), .sel(in_9));
  Multiplexer #(.select(2), .enable("false")) multiplexer_4 (
    .in0(and_4_out), .in1(or_4_out), .in2(xor_4_out), .in3(not_4_out), .out(Y3), .sel(in_9));

  // Notes on the sheet:
  //   23CS037
endmodule

module _8bit_Logical_4 (
  input  A0,
  input  B0,
  input  A1,
  input  B1,
  input  A2,
  input  B2,
  input  A3,
  input  B3,
  input  A4,
  input  B4,
  input  A5,
  input  B5,
  input  A6,
  input  B6,
  input  A7,
  input  B7,
  input  [1:0] in_17,
  output Y0,
  output Y1,
  output Y2,
  output Y3,
  output Y4,
  output Y5,
  output Y6,
  output Y7
);

  wire and_1_out, and_2_out, and_3_out, and_4_out, and_5_out, and_6_out, and_7_out, and_8_out, not_1_out,
       not_2_out, not_3_out, not_4_out, not_5_out, not_6_out, not_7_out, not_8_out, or_1_out, or_2_out,
       or_3_out, or_4_out, or_5_out, or_6_out, or_7_out, or_8_out, xor_1_out, xor_2_out, xor_3_out,
       xor_4_out, xor_5_out, xor_6_out, xor_7_out, xor_8_out;

  and and_1 (and_1_out, A0, B0);
  or or_1 (or_1_out, A0, B0);
  xor xor_1 (xor_1_out, A0, B0);
  not not_1 (not_1_out, A0);
  and and_2 (and_2_out, A1, B1);
  or or_2 (or_2_out, A1, B1);
  xor xor_2 (xor_2_out, A1, B1);
  not not_2 (not_2_out, A1);
  and and_3 (and_3_out, A2, B2);
  or or_3 (or_3_out, A2, B2);
  xor xor_3 (xor_3_out, A2, B2);
  not not_3 (not_3_out, A2);
  and and_4 (and_4_out, A3, B3);
  or or_4 (or_4_out, A3, B3);
  xor xor_4 (xor_4_out, A3, B3);
  not not_4 (not_4_out, A3);
  and and_5 (and_5_out, A4, B4);
  or or_5 (or_5_out, A4, B4);
  xor xor_5 (xor_5_out, A4, B4);
  not not_5 (not_5_out, A4);
  and and_6 (and_6_out, A5, B5);
  or or_6 (or_6_out, A5, B5);
  xor xor_6 (xor_6_out, A5, B5);
  not not_6 (not_6_out, A5);
  and and_7 (and_7_out, A6, B6);
  or or_7 (or_7_out, A6, B6);
  xor xor_7 (xor_7_out, A6, B6);
  not not_7 (not_7_out, A6);
  and and_8 (and_8_out, A7, B7);
  or or_8 (or_8_out, A7, B7);
  xor xor_8 (xor_8_out, A7, B7);
  not not_8 (not_8_out, A7);
  Multiplexer #(.select(2), .enable("false")) multiplexer_1 (
    .in0(and_1_out), .in1(or_1_out), .in2(xor_1_out), .in3(not_1_out), .out(Y0), .sel(in_17));
  Multiplexer #(.select(2), .enable("false")) multiplexer_2 (
    .in0(and_2_out), .in1(or_2_out), .in2(xor_2_out), .in3(not_2_out), .out(Y1), .sel(in_17));
  Multiplexer #(.select(2), .enable("false")) multiplexer_3 (
    .in0(and_3_out), .in1(or_3_out), .in2(xor_3_out), .in3(not_3_out), .out(Y2), .sel(in_17));
  Multiplexer #(.select(2), .enable("false")) multiplexer_4 (
    .in0(and_4_out), .in1(or_4_out), .in2(xor_4_out), .in3(not_4_out), .out(Y3), .sel(in_17));
  Multiplexer #(.select(2), .enable("false")) multiplexer_5 (
    .in0(and_5_out), .in1(or_5_out), .in2(xor_5_out), .in3(not_5_out), .out(Y4), .sel(in_17));
  Multiplexer #(.select(2), .enable("false")) multiplexer_6 (
    .in0(and_6_out), .in1(or_6_out), .in2(xor_6_out), .in3(not_6_out), .out(Y5), .sel(in_17));
  Multiplexer #(.select(2), .enable("false")) multiplexer_7 (
    .in0(and_7_out), .in1(or_7_out), .in2(xor_7_out), .in3(not_7_out), .out(Y6), .sel(in_17));
  Multiplexer #(.select(2), .enable("false")) multiplexer_8 (
    .in0(and_8_out), .in1(or_8_out), .in2(xor_8_out), .in3(not_8_out), .out(Y7), .sel(in_17));

  // Notes on the sheet:
  //   23CS037
endmodule

module _2bit_Logical_16 (
  input  B,
  input  A,
  input  [3:0] in_3,
  input  B_2,
  input  A_2,
  output F0,
  output F1
);

  wire and_1_out, and_2_out, and_3_out, and_4_out, and_5_out, and_6_out, and_7_out, and_8_out, nand_1_out,
       nand_2_out, nor_1_out, nor_2_out, not_1_out, not_2_out, not_3_out, not_4_out, or_1_out, or_2_out,
       or_3_out, or_4_out, or_5_out, or_6_out, or_7_out, or_8_out, xnor_1_out, xnor_2_out, xor_1_out,
       xor_2_out;

  not not_1 (not_1_out, B);
  not not_2 (not_2_out, A);
  not not_3 (not_3_out, B_2);
  and and_1 (and_1_out, A, 1'b0);
  and and_2 (and_2_out, A, B);
  and and_3 (and_3_out, A, not_1_out);
  and and_4 (and_4_out, not_2_out, B);
  xor xor_1 (xor_1_out, A, B);
  or or_1 (or_1_out, A, B);
  nor nor_1 (nor_1_out, A, B);
  xnor xnor_1 (xnor_1_out, A, B);
  or or_2 (or_2_out, A, not_1_out);
  or or_3 (or_3_out, not_2_out, B);
  nand nand_1 (nand_1_out, A, B);
  or or_4 (or_4_out, A, 1'b1);
  not not_4 (not_4_out, A_2);
  and and_5 (and_5_out, A_2, 1'b0);
  and and_6 (and_6_out, A_2, B_2);
  and and_7 (and_7_out, A_2, not_3_out);
  and and_8 (and_8_out, not_4_out, B_2);
  xor xor_2 (xor_2_out, A_2, B_2);
  or or_5 (or_5_out, A_2, B_2);
  nor nor_2 (nor_2_out, A_2, B_2);
  xnor xnor_2 (xnor_2_out, A_2, B_2);
  or or_6 (or_6_out, A_2, not_3_out);
  or or_7 (or_7_out, not_4_out, B_2);
  nand nand_2 (nand_2_out, A_2, B_2);
  or or_8 (or_8_out, A_2, 1'b1);
  Multiplexer #(.select(4), .enable("false")) multiplexer_1 (
    .in0(and_1_out), .in1(and_2_out), .in2(and_3_out), .in3(A), .in4(and_4_out), .in5(B), .in6(xor_1_out),
    .in7(or_1_out), .in8(nor_1_out), .in9(xnor_1_out), .in10(not_1_out), .in11(or_2_out), .in12(not_2_out),
    .in13(or_3_out), .in14(nand_1_out), .in15(or_4_out), .out(F0), .sel(in_3));
  Multiplexer #(.select(4), .enable("false")) multiplexer_2 (
    .in0(and_5_out), .in1(and_6_out), .in2(and_7_out), .in3(A_2), .in4(and_8_out), .in5(B_2),
    .in6(xor_2_out), .in7(or_5_out), .in8(nor_2_out), .in9(xnor_2_out), .in10(not_3_out), .in11(or_6_out),
    .in12(not_4_out), .in13(or_7_out), .in14(nand_2_out), .in15(or_8_out), .out(F1), .sel(in_3));

  // Notes on the sheet:
  //   23CS037
endmodule

module _4bit_biDirectionalShifter (
  input  [3:0] A3A2A1A0,
  input  in_2,
  output [3:0] F
);

  Multiplexer #(.enable("false")) multiplexer_1 (.in0(1'b0), .in1(A3A2A1A0[2]), .out(F[3]), .sel(in_2));
  Multiplexer #(.enable("false")) multiplexer_2 (.in0(A3A2A1A0[3]), .in1(A3A2A1A0[1]), .out(F[2]), .sel(in_2));
  Multiplexer #(.enable("false")) multiplexer_3 (.in0(A3A2A1A0[1]), .in1(1'b0), .out(F[0]), .sel(in_2));
  Multiplexer #(.enable("false")) multiplexer_4 (.in0(A3A2A1A0[2]), .in1(A3A2A1A0[0]), .out(F[1]), .sel(in_2));

  // Notes on the sheet:
  //   serialInputRight
  //   23CS037
  //   serialInputLeft
endmodule

module _8bit_biDirectionalShifter (
  input  [7:0] A7A6A5A4A3A2A1A0,
  input  in_2,
  output [7:0] F
);

  Multiplexer #(.enable("false")) multiplexer_1 (.in0(1'b0), .in1(A7A6A5A4A3A2A1A0[6]), .out(F[7]), .sel(in_2));
  Multiplexer #(.enable("false")) multiplexer_2 (
    .in0(A7A6A5A4A3A2A1A0[6]), .in1(A7A6A5A4A3A2A1A0[4]), .out(F[5]), .sel(in_2));
  Multiplexer #(.enable("false")) multiplexer_3 (
    .in0(A7A6A5A4A3A2A1A0[7]), .in1(A7A6A5A4A3A2A1A0[5]), .out(F[6]), .sel(in_2));
  Multiplexer #(.enable("false")) multiplexer_4 (
    .in0(A7A6A5A4A3A2A1A0[5]), .in1(A7A6A5A4A3A2A1A0[3]), .out(F[4]), .sel(in_2));
  Multiplexer #(.enable("false")) multiplexer_5 (
    .in0(A7A6A5A4A3A2A1A0[3]), .in1(A7A6A5A4A3A2A1A0[1]), .out(F[2]), .sel(in_2));
  Multiplexer #(.enable("false")) multiplexer_6 (
    .in0(A7A6A5A4A3A2A1A0[4]), .in1(A7A6A5A4A3A2A1A0[2]), .out(F[3]), .sel(in_2));
  Multiplexer #(.enable("false")) multiplexer_7 (
    .in0(A7A6A5A4A3A2A1A0[2]), .in1(A7A6A5A4A3A2A1A0[0]), .out(F[1]), .sel(in_2));
  Multiplexer #(.enable("false")) multiplexer_8 (.in0(A7A6A5A4A3A2A1A0[1]), .in1(1'b0), .out(F[0]), .sel(in_2));

  // Notes on the sheet:
  //   serialInputRight
  //   23CS037
  //   serialInputLeft
endmodule

module _1bit_ALU (
  input  [3:0] in_1,
  input  Cin,
  input  A,
  input  B,
  input  SH,
  output F,
  output Cout
);

  wire n1bit_arithmatic_1_s0, n1bit_logical_4_1_y0;

  _1bit_Arithmatic u_1bit_arithmatic_1 (
    .Cin(Cin), .A0(A), .B0(B), .in_4(in_1[1:0]), .S0(n1bit_arithmatic_1_s0), .Cout(Cout));
  _1bit_Logical_4 u_1bit_logical_4_1 (.A0(A), .B0(B), .in_3(in_1[1:0]), .Y0(n1bit_logical_4_1_y0));
  Multiplexer #(.select(2), .enable("false")) multiplexer_1 (
    .in0(n1bit_arithmatic_1_s0), .in1(n1bit_logical_4_1_y0), .in2(SH), .in3(SH), .out(F), .sel(in_1[3:2]));

  // Notes on the sheet:
  //   23CS037
endmodule

module _2bit_ALU (
  input  [1:0] B1_B0,
  input  [1:0] A1_A0,
  input  [3:0] Selectline,
  input  Cin,
  input  in_5,
  output [1:0] F,
  output Cout
);

  wire n1bit_arithmatic_1_cout, n1bit_arithmatic_1_s0, n1bit_arithmatic_2_s0, n1bit_logical_4_1_y0,
       n1bit_logical_4_2_y0;

  _1bit_Arithmatic u_1bit_arithmatic_1 (
    .Cin(Cin), .A0(A1_A0[0]), .B0(B1_B0[0]), .in_4(Selectline[1:0]), .S0(n1bit_arithmatic_1_s0),
    .Cout(n1bit_arithmatic_1_cout));
  _1bit_Logical_4 u_1bit_logical_4_1 (.A0(A1_A0[0]), .B0(B1_B0[0]), .in_3(Selectline[1:0]), .Y0(n1bit_logical_4_1_y0));
  _1bit_Arithmatic u_1bit_arithmatic_2 (
    .Cin(n1bit_arithmatic_1_cout), .A0(A1_A0[1]), .B0(B1_B0[1]), .in_4(Selectline[1:0]),
    .S0(n1bit_arithmatic_2_s0), .Cout(Cout));
  _1bit_Logical_4 u_1bit_logical_4_2 (.A0(A1_A0[1]), .B0(B1_B0[1]), .in_3(Selectline[1:0]), .Y0(n1bit_logical_4_2_y0));
  Multiplexer #(.select(2), .enable("false")) multiplexer_1 (
    .in0(n1bit_arithmatic_1_s0), .in1(n1bit_logical_4_1_y0), .in2(A1_A0[1]), .in3(in_5), .out(F[0]),
    .sel(Selectline[3:2]));
  Multiplexer #(.select(2), .enable("false")) multiplexer_2 (
    .in0(n1bit_arithmatic_2_s0), .in1(n1bit_logical_4_2_y0), .in2(in_5), .in3(A1_A0[0]), .out(F[1]),
    .sel(Selectline[3:2]));

  // Notes on the sheet:
  //   23CS037
  //   Operation Selector
  //   Circuit Selector
endmodule

module _4bit_ALU (
  input  [3:0] Selectline,
  input  Cin,
  input  A0,
  input  B0,
  input  A1,
  input  B1,
  input  A2,
  input  B2,
  input  A3,
  input  B3,
  input  in_11,
  output [3:0] F,
  output Cout
);

  wire n1bit_arithmatic_1_cout, n1bit_arithmatic_1_s0, n1bit_arithmatic_2_cout, n1bit_arithmatic_2_s0,
       n1bit_arithmatic_3_cout, n1bit_arithmatic_3_s0, n1bit_arithmatic_4_s0, n1bit_logical_4_1_y0,
       n1bit_logical_4_2_y0, n1bit_logical_4_3_y0, n1bit_logical_4_4_y0;

  _1bit_Arithmatic u_1bit_arithmatic_1 (
    .Cin(Cin), .A0(A0), .B0(B0), .in_4(Selectline[1:0]), .S0(n1bit_arithmatic_1_s0),
    .Cout(n1bit_arithmatic_1_cout));
  _1bit_Logical_4 u_1bit_logical_4_1 (.A0(A0), .B0(B0), .in_3(Selectline[1:0]), .Y0(n1bit_logical_4_1_y0));
  _1bit_Arithmatic u_1bit_arithmatic_2 (
    .Cin(n1bit_arithmatic_1_cout), .A0(A1), .B0(B1), .in_4(Selectline[1:0]), .S0(n1bit_arithmatic_2_s0),
    .Cout(n1bit_arithmatic_2_cout));
  _1bit_Logical_4 u_1bit_logical_4_2 (.A0(A1), .B0(B1), .in_3(Selectline[1:0]), .Y0(n1bit_logical_4_2_y0));
  _1bit_Arithmatic u_1bit_arithmatic_3 (
    .Cin(n1bit_arithmatic_2_cout), .A0(A2), .B0(B2), .in_4(Selectline[1:0]), .S0(n1bit_arithmatic_3_s0),
    .Cout(n1bit_arithmatic_3_cout));
  _1bit_Logical_4 u_1bit_logical_4_3 (.A0(A2), .B0(B2), .in_3(Selectline[1:0]), .Y0(n1bit_logical_4_3_y0));
  _1bit_Arithmatic u_1bit_arithmatic_4 (
    .Cin(n1bit_arithmatic_3_cout), .A0(A3), .B0(B3), .in_4(Selectline[1:0]), .S0(n1bit_arithmatic_4_s0),
    .Cout(Cout));
  _1bit_Logical_4 u_1bit_logical_4_4 (.A0(A3), .B0(B3), .in_3(Selectline[1:0]), .Y0(n1bit_logical_4_4_y0));
  Multiplexer #(.select(2), .enable("false")) multiplexer_1 (
    .in0(n1bit_arithmatic_1_s0), .in1(n1bit_logical_4_1_y0), .in2(A1), .in3(in_11), .out(F[0]),
    .sel(Selectline[3:2]));
  Multiplexer #(.select(2), .enable("false")) multiplexer_2 (
    .in0(n1bit_arithmatic_2_s0), .in1(n1bit_logical_4_2_y0), .in2(A2), .in3(A0), .out(F[1]),
    .sel(Selectline[3:2]));
  Multiplexer #(.select(2), .enable("false")) multiplexer_3 (
    .in0(n1bit_arithmatic_3_s0), .in1(n1bit_logical_4_3_y0), .in2(A3), .in3(A1), .out(F[2]),
    .sel(Selectline[3:2]));
  Multiplexer #(.select(2), .enable("false")) multiplexer_4 (
    .in0(n1bit_arithmatic_4_s0), .in1(n1bit_logical_4_4_y0), .in2(in_11), .in3(A2), .out(F[3]),
    .sel(Selectline[3:2]));

  // Notes on the sheet:
  //   23CS037
  //   Operation Selector
  //   Circuit Selector
endmodule

module _8bit_ALU (
  input  [3:0] Selectline,
  input  [7:0] B7B6B5B4B3B2B1B0,
  input  [7:0] A7A6A5A4A3A2A1A0,
  input  Cin,
  input  SHL,
  input  SHR,
  output [7:0] F,
  output Cout
);

  wire n1bit_arithmatic_1_cout, n1bit_arithmatic_1_s0, n1bit_arithmatic_2_cout, n1bit_arithmatic_2_s0,
       n1bit_arithmatic_3_cout, n1bit_arithmatic_3_s0, n1bit_arithmatic_4_cout, n1bit_arithmatic_4_s0,
       n1bit_arithmatic_5_cout, n1bit_arithmatic_5_s0, n1bit_arithmatic_6_cout, n1bit_arithmatic_6_s0,
       n1bit_arithmatic_7_cout, n1bit_arithmatic_7_s0, n1bit_arithmatic_8_s0, n1bit_logical_4_1_y0,
       n1bit_logical_4_2_y0, n1bit_logical_4_3_y0, n1bit_logical_4_4_y0, n1bit_logical_4_5_y0,
       n1bit_logical_4_6_y0, n1bit_logical_4_7_y0, n1bit_logical_4_8_y0;

  _1bit_Arithmatic u_1bit_arithmatic_1 (
    .Cin(Cin), .A0(A7A6A5A4A3A2A1A0[0]), .B0(B7B6B5B4B3B2B1B0[0]), .in_4(Selectline[1:0]),
    .S0(n1bit_arithmatic_1_s0), .Cout(n1bit_arithmatic_1_cout));
  _1bit_Logical_4 u_1bit_logical_4_1 (
    .A0(A7A6A5A4A3A2A1A0[0]), .B0(B7B6B5B4B3B2B1B0[0]), .in_3(Selectline[1:0]), .Y0(n1bit_logical_4_1_y0));
  _1bit_Arithmatic u_1bit_arithmatic_2 (
    .Cin(n1bit_arithmatic_1_cout), .A0(A7A6A5A4A3A2A1A0[1]), .B0(B7B6B5B4B3B2B1B0[1]),
    .in_4(Selectline[1:0]), .S0(n1bit_arithmatic_2_s0), .Cout(n1bit_arithmatic_2_cout));
  _1bit_Logical_4 u_1bit_logical_4_2 (
    .A0(A7A6A5A4A3A2A1A0[1]), .B0(B7B6B5B4B3B2B1B0[1]), .in_3(Selectline[1:0]), .Y0(n1bit_logical_4_2_y0));
  _1bit_Arithmatic u_1bit_arithmatic_3 (
    .Cin(n1bit_arithmatic_2_cout), .A0(A7A6A5A4A3A2A1A0[2]), .B0(B7B6B5B4B3B2B1B0[2]),
    .in_4(Selectline[1:0]), .S0(n1bit_arithmatic_3_s0), .Cout(n1bit_arithmatic_3_cout));
  _1bit_Logical_4 u_1bit_logical_4_3 (
    .A0(A7A6A5A4A3A2A1A0[2]), .B0(B7B6B5B4B3B2B1B0[2]), .in_3(Selectline[1:0]), .Y0(n1bit_logical_4_3_y0));
  _1bit_Arithmatic u_1bit_arithmatic_4 (
    .Cin(n1bit_arithmatic_3_cout), .A0(A7A6A5A4A3A2A1A0[3]), .B0(B7B6B5B4B3B2B1B0[3]),
    .in_4(Selectline[1:0]), .S0(n1bit_arithmatic_4_s0), .Cout(n1bit_arithmatic_4_cout));
  _1bit_Logical_4 u_1bit_logical_4_4 (
    .A0(A7A6A5A4A3A2A1A0[3]), .B0(B7B6B5B4B3B2B1B0[3]), .in_3(Selectline[1:0]), .Y0(n1bit_logical_4_4_y0));
  _1bit_Arithmatic u_1bit_arithmatic_5 (
    .Cin(n1bit_arithmatic_4_cout), .A0(A7A6A5A4A3A2A1A0[4]), .B0(B7B6B5B4B3B2B1B0[4]),
    .in_4(Selectline[1:0]), .S0(n1bit_arithmatic_5_s0), .Cout(n1bit_arithmatic_5_cout));
  _1bit_Logical_4 u_1bit_logical_4_5 (
    .A0(A7A6A5A4A3A2A1A0[4]), .B0(B7B6B5B4B3B2B1B0[4]), .in_3(Selectline[1:0]), .Y0(n1bit_logical_4_5_y0));
  _1bit_Arithmatic u_1bit_arithmatic_6 (
    .Cin(n1bit_arithmatic_5_cout), .A0(A7A6A5A4A3A2A1A0[5]), .B0(B7B6B5B4B3B2B1B0[5]),
    .in_4(Selectline[1:0]), .S0(n1bit_arithmatic_6_s0), .Cout(n1bit_arithmatic_6_cout));
  _1bit_Logical_4 u_1bit_logical_4_6 (
    .A0(A7A6A5A4A3A2A1A0[5]), .B0(B7B6B5B4B3B2B1B0[5]), .in_3(Selectline[1:0]), .Y0(n1bit_logical_4_6_y0));
  _1bit_Arithmatic u_1bit_arithmatic_7 (
    .Cin(n1bit_arithmatic_6_cout), .A0(A7A6A5A4A3A2A1A0[6]), .B0(B7B6B5B4B3B2B1B0[6]),
    .in_4(Selectline[1:0]), .S0(n1bit_arithmatic_7_s0), .Cout(n1bit_arithmatic_7_cout));
  _1bit_Logical_4 u_1bit_logical_4_7 (
    .A0(A7A6A5A4A3A2A1A0[6]), .B0(B7B6B5B4B3B2B1B0[6]), .in_3(Selectline[1:0]), .Y0(n1bit_logical_4_7_y0));
  _1bit_Arithmatic u_1bit_arithmatic_8 (
    .Cin(n1bit_arithmatic_7_cout), .A0(A7A6A5A4A3A2A1A0[7]), .B0(B7B6B5B4B3B2B1B0[7]),
    .in_4(Selectline[1:0]), .S0(n1bit_arithmatic_8_s0), .Cout(Cout));
  _1bit_Logical_4 u_1bit_logical_4_8 (
    .A0(A7A6A5A4A3A2A1A0[7]), .in_3(Selectline[1:0]), .Y0(n1bit_logical_4_8_y0));  // open: B0
  Multiplexer #(.select(2), .enable("false")) multiplexer_1 (
    .in0(n1bit_arithmatic_1_s0), .in1(n1bit_logical_4_1_y0), .in2(A7A6A5A4A3A2A1A0[1]), .in3(SHL),
    .out(F[0]), .sel(Selectline[3:2]));
  Multiplexer #(.select(2), .enable("false")) multiplexer_2 (
    .in0(n1bit_arithmatic_2_s0), .in1(n1bit_logical_4_2_y0), .in2(A7A6A5A4A3A2A1A0[2]),
    .in3(A7A6A5A4A3A2A1A0[0]), .out(F[1]), .sel(Selectline[3:2]));
  Multiplexer #(.select(2), .enable("false")) multiplexer_3 (
    .in0(n1bit_arithmatic_3_s0), .in1(n1bit_logical_4_3_y0), .in2(A7A6A5A4A3A2A1A0[3]),
    .in3(A7A6A5A4A3A2A1A0[1]), .out(F[2]), .sel(Selectline[3:2]));
  Multiplexer #(.select(2), .enable("false")) multiplexer_4 (
    .in0(n1bit_arithmatic_4_s0), .in1(n1bit_logical_4_4_y0), .in2(A7A6A5A4A3A2A1A0[4]),
    .in3(A7A6A5A4A3A2A1A0[2]), .out(F[3]), .sel(Selectline[3:2]));
  Multiplexer #(.select(2), .enable("false")) multiplexer_5 (
    .in0(n1bit_arithmatic_5_s0), .in1(n1bit_logical_4_5_y0), .in2(A7A6A5A4A3A2A1A0[5]),
    .in3(A7A6A5A4A3A2A1A0[3]), .out(F[4]), .sel(Selectline[3:2]));
  Multiplexer #(.select(2), .enable("false")) multiplexer_6 (
    .in0(n1bit_arithmatic_6_s0), .in1(n1bit_logical_4_6_y0), .in2(A7A6A5A4A3A2A1A0[6]),
    .in3(A7A6A5A4A3A2A1A0[4]), .out(F[5]), .sel(Selectline[3:2]));
  Multiplexer #(.select(2), .enable("false")) multiplexer_7 (
    .in0(n1bit_arithmatic_7_s0), .in1(n1bit_logical_4_7_y0), .in2(A7A6A5A4A3A2A1A0[7]),
    .in3(A7A6A5A4A3A2A1A0[5]), .out(F[6]), .sel(Selectline[3:2]));
  Multiplexer #(.select(2), .enable("false")) multiplexer_8 (
    .in0(n1bit_arithmatic_8_s0), .in1(n1bit_logical_4_8_y0), .in2(SHR), .in3(A7A6A5A4A3A2A1A0[6]),
    .out(F[7]), .sel(Selectline[3:2]));

  // Notes on the sheet:
  //   23CS037
  //   Operation Selector
  //   Circuit Selector
endmodule

module _16bit_ALU (
  input  [3:0] SelectLine,
  input  C_in,
  input  [15:0] A,
  input  [15:0] B,
  input  SHL,
  input  SHR,
  output [15:0] AC,
  output Cout
);

  wire n8bit_alu_1_cout;

  _8bit_ALU u_8bit_alu_1 (
    .B7B6B5B4B3B2B1B0(B[7:0]), .A7A6A5A4A3A2A1A0(A[7:0]), .Cin(C_in), .Selectline(SelectLine), .SHL(A[7]),
    .SHR(SHR), .F(AC[7:0]), .Cout(n8bit_alu_1_cout));
  _8bit_ALU u_8bit_alu_2 (
    .B7B6B5B4B3B2B1B0(B[15:8]), .A7A6A5A4A3A2A1A0(A[15:8]), .Cin(n8bit_alu_1_cout), .Selectline(SelectLine),
    .SHL(SHL), .SHR(A[8]), .F(AC[15:8]), .Cout(Cout));

  // Notes on the sheet:
  //   23CS037
endmodule

module _16bit_CommonBusSystem (
  input  [11:0] ADD_EXT,
  input  MEM_ADD,
  input  [15:0] DATA_EXT,
  input  MEM_DATA,
  input  MEM_WRT,
  input  MEM_CS,
  input  MEM_RD,
  input  MEM_CLR,
  input  LD_AR,
  input  INR_AR,
  input  CLR_AR,
  input  LD_PC,
  input  INR_PC,
  input  CLR_PC,
  input  LD_DR,
  input  [3:0] SEL,
  input  C_in,
  input  INR_DR,
  input  [1:0] SEL_A,
  input  CLR_DR,
  input  LD_AC,
  input  SHL,
  input  SHR,
  input  INR_AC,
  input  CLR_AC,
  input  [1:0] SEL_B,
  input  [7:0] INPR,
  input  [2:0] SEL_2,
  input  EN_IR,
  input  CLR_IR,
  input  LD_TR,
  input  INR_TR,
  input  CLR_TR,
  input  EN_OUTR,
  input  CLR_OUTR,
  output E,
  output [15:0] CB
);

  wire CB_CLK_out, MEM_Clk_out, SYS_CLK_out;
  wire [11:0] AR_q, multiplexer_3_out, PC_q;
  wire [15:0] AC_q, DR_q, IR_q, multiplexer_1_out, multiplexer_2_out, multiplexer_4_out, multiplexer_5_out,
       n16bit_alu_1_ac, ram_1_data, TR_q;

  Multiplexer #(.select(2), .width(16), .enable("false")) multiplexer_1 (
    .in0(AC_q), .in1(DR_q), .in2({{8{1'b0}}, INPR}), .in3(AC_q), .out(multiplexer_1_out), .sel(SEL_A));
  Multiplexer #(.select(2), .width(16), .enable("false")) multiplexer_2 (
    .in0(AC_q), .in1(DR_q), .in2({{8{1'b0}}, INPR}), .in3(AC_q), .out(multiplexer_2_out), .sel(SEL_B));
  Clock MEM_Clk (.out(MEM_Clk_out));
  _16bit_ALU u_16bit_alu_1 (
    .A(multiplexer_1_out), .B(multiplexer_2_out), .SelectLine(SEL), .C_in(C_in), .SHL(SHL), .SHR(SHR),
    .AC(n16bit_alu_1_ac), .Cout(E));
  Multiplexer #(.width(12), .enable("false")) multiplexer_3 (
    .in0(AR_q), .in1(ADD_EXT), .out(multiplexer_3_out), .sel(MEM_ADD));
  Multiplexer #(.width(16), .enable("false")) multiplexer_4 (
    .in0(CB), .in1(DATA_EXT), .out(multiplexer_4_out), .sel(MEM_DATA));
  Clock SYS_CLK (.out(SYS_CLK_out));
  Counter #(.width(12), .max('hfff)) AR (
    .load(LD_AR), .D(CB[11:0]), .count(INR_AR), .Q(AR_q), .clk(SYS_CLK_out), .clr(CLR_AR));  // open: carry
  Counter #(.width(12), .max('hfff)) PC (
    .load(LD_PC), .D(CB[11:0]), .count(INR_PC), .Q(PC_q), .clk(SYS_CLK_out), .clr(CLR_PC));  // open: carry
  Counter #(.width(16), .max('hffff)) DR (
    .load(LD_DR), .D(CB), .count(INR_DR), .Q(DR_q), .clk(SYS_CLK_out), .clr(CLR_DR));  // open: carry
  Counter #(.width(16), .max('hffff)) AC (
    .load(LD_AC), .D(n16bit_alu_1_ac), .count(INR_AC), .Q(AC_q), .clk(SYS_CLK_out), .clr(CLR_AC));  // open: carry
  Register #(.width(16)) IR (.D(CB), .en(EN_IR), .Q(IR_q), .clk(SYS_CLK_out), .clr(CLR_IR));
  Counter #(.width(16), .max('hffff)) TR (
    .load(LD_TR), .D(CB), .count(INR_TR), .Q(TR_q), .clk(SYS_CLK_out), .clr(CLR_TR));  // open: carry
  Register OUTR (.D(CB[7:0]), .en(EN_OUTR), .clk(SYS_CLK_out), .clr(CLR_OUTR));  // open: Q
  RAM #(.addrWidth(12), .dataWidth(16), .bus("separate")) ram_1 (
    .addr(multiplexer_3_out), .din(multiplexer_4_out), .data(ram_1_data), .str(MEM_WRT), .sel(MEM_CS),
    .clk(MEM_Clk_out), .ld(MEM_RD), .clr(MEM_CLR));
  Multiplexer #(.select(3), .width(16), .enable("false")) multiplexer_5 (
    .in1({4'b0000, AR_q}), .in2({4'b0000, PC_q}), .in3(DR_q), .in4(AC_q), .in5(IR_q), .in6(TR_q),
    .in7(ram_1_data), .out(multiplexer_5_out), .sel(SEL_2));  // open: in0
  Register #(.width(16)) register_1 (.D(multiplexer_5_out), .en(1'b1), .Q(CB), .clk(CB_CLK_out), .clr(1'b0));
  Clock CB_CLK (.out(CB_CLK_out));

  // Notes on the sheet:
  //   23CS037
endmodule
